// Logisim project 2107028 2107027 (CLOCK PROJECT).circ as structural Verilog: 7 circuits, main circuit main
module main (
);

  wire bcd_to_7_1_a_2, bcd_to_7_1_b_2, bcd_to_7_1_c_2, bcd_to_7_1_d_2, bcd_to_7_1_e, bcd_to_7_1_f,
       bcd_to_7_1_g, bcd_to_7_2_a_2, bcd_to_7_2_b_2, bcd_to_7_2_c_2, bcd_to_7_2_d_2, bcd_to_7_2_e,
       bcd_to_7_2_f, bcd_to_7_2_g, bcd_to_7_3_a_2, bcd_to_7_3_b_2, bcd_to_7_3_c_2, bcd_to_7_3_d_2,
       bcd_to_7_3_e, bcd_to_7_3_f, bcd_to_7_3_g, bcd_to_7_4_a_2, bcd_to_7_4_b_2, bcd_to_7_4_c_2,
       bcd_to_7_4_d_2, bcd_to_7_4_e, bcd_to_7_4_f, bcd_to_7_4_g, bcd_to_7_5_a_2, bcd_to_7_5_b_2,
       bcd_to_7_5_c_2, bcd_to_7_5_d_2, bcd_to_7_5_e, bcd_to_7_5_f, bcd_to_7_5_g, bcd_to_7_6_a_2,
       bcd_to_7_6_b_2, bcd_to_7_6_c_2, bcd_to_7_6_d_2, bcd_to_7_6_e, bcd_to_7_6_f, bcd_to_7_6_g, clock_1_out,
       hour_1_lsb_right, hour_1_lsb_right_2, hour_1_msb_left, hour_1_msb_right, hour_1_out_3, hour_1_out_4,
       hour_1_out_7, hour_1_out_8, minute_1_clock_puls_for_hour, minute_1_lsb_minute_5,
       minute_1_lsb_minute_10, minute_1_msb_minute_5, minute_1_msb_minute_10, minute_1_out_3, minute_1_out_4,
       minute_1_out_7, minute_1_out_8, second_1_clock_puls_for_minute, second_1_lsb_5, second_1_lsb_10,
       second_1_msb_5, second_1_msb_10, second_1_out_3, second_1_out_4, second_1_out_7, second_1_out_8;

  Clock clock_1 (.out(clock_1_out));
  second second_1 (
    .clock(clock_1_out), .clock_puls_for_minute(second_1_clock_puls_for_minute), .msb_10(second_1_msb_10),
    .out_3(second_1_out_3), .out_4(second_1_out_4), .lsb_10(second_1_lsb_10), .msb_5(second_1_msb_5),
    .out_7(second_1_out_7), .out_8(second_1_out_8), .lsb_5(second_1_lsb_5));
  minute minute_1 (
    .clock(second_1_clock_puls_for_minute), .clock_puls_for_hour(minute_1_clock_puls_for_hour),
    .msb_minute_10(minute_1_msb_minute_10), .out_3(minute_1_out_3), .out_4(minute_1_out_4),
    .lsb_minute_10(minute_1_lsb_minute_10), .msb_minute_5(minute_1_msb_minute_5), .out_7(minute_1_out_7),
    .out_8(minute_1_out_8), .lsb_minute_5(minute_1_lsb_minute_5));
  hour hour_1 (
    .clock(minute_1_clock_puls_for_hour), .MSB_right(hour_1_msb_right), .out_3(hour_1_out_3),
    .out_4(hour_1_out_4), .LSB_right(hour_1_lsb_right), .MSB_left(hour_1_msb_left), .out_7(hour_1_out_7),
    .out_8(hour_1_out_8), .LSB_right_2(hour_1_lsb_right_2));
  bcd_to_7 bcd_to_7_1 (
    .A(second_1_msb_10), .B(second_1_out_3), .C(second_1_out_4), .D(second_1_lsb_10), .a_2(bcd_to_7_1_a_2),
    .b_2(bcd_to_7_1_b_2), .c_2(bcd_to_7_1_c_2), .d_2(bcd_to_7_1_d_2), .e(bcd_to_7_1_e), .f(bcd_to_7_1_f),
    .g(bcd_to_7_1_g));
  bcd_to_7 bcd_to_7_2 (
    .A(second_1_msb_5), .B(second_1_out_7), .C(second_1_out_8), .D(second_1_lsb_5), .a_2(bcd_to_7_2_a_2),
    .b_2(bcd_to_7_2_b_2), .c_2(bcd_to_7_2_c_2), .d_2(bcd_to_7_2_d_2), .e(bcd_to_7_2_e), .f(bcd_to_7_2_f),
    .g(bcd_to_7_2_g));
  bcd_to_7 bcd_to_7_3 (
    .A(minute_1_msb_minute_10), .B(minute_1_out_3), .C(minute_1_out_4), .D(minute_1_lsb_minute_10),
    .a_2(bcd_to_7_3_a_2), .b_2(bcd_to_7_3_b_2), .c_2(bcd_to_7_3_c_2), .d_2(bcd_to_7_3_d_2), .e(bcd_to_7_3_e),
    .f(bcd_to_7_3_f), .g(bcd_to_7_3_g));
  bcd_to_7 bcd_to_7_4 (
    .A(minute_1_msb_minute_5), .B(minute_1_out_7), .C(minute_1_out_8), .D(minute_1_lsb_minute_5),
    .a_2(bcd_to_7_4_a_2), .b_2(bcd_to_7_4_b_2), .c_2(bcd_to_7_4_c_2), .d_2(bcd_to_7_4_d_2), .e(bcd_to_7_4_e),
    .f(bcd_to_7_4_f), .g(bcd_to_7_4_g));
  bcd_to_7 bcd_to_7_5 (
    .A(hour_1_msb_right), .B(hour_1_out_3), .C(hour_1_out_4), .D(hour_1_lsb_right), .a_2(bcd_to_7_5_a_2),
    .b_2(bcd_to_7_5_b_2), .c_2(bcd_to_7_5_c_2), .d_2(bcd_to_7_5_d_2), .e(bcd_to_7_5_e), .f(bcd_to_7_5_f),
    .g(bcd_to_7_5_g));
  bcd_to_7 bcd_to_7_6 (
    .A(hour_1_msb_left), .B(hour_1_out_7), .C(hour_1_out_8), .D(hour_1_lsb_right_2), .a_2(bcd_to_7_6_a_2),
    .b_2(bcd_to_7_6_b_2), .c_2(bcd_to_7_6_c_2), .d_2(bcd_to_7_6_d_2), .e(bcd_to_7_6_e), .f(bcd_to_7_6_f),
    .g(bcd_to_7_6_g));
  _7_Segment_Display u_7_segment_display_1 (
    .g(bcd_to_7_5_g), .f(bcd_to_7_5_f), .a(bcd_to_7_5_a_2), .b(bcd_to_7_5_b_2), .e(bcd_to_7_5_e),
    .d(bcd_to_7_5_d_2), .c(bcd_to_7_5_c_2));  // open: dp
  _7_Segment_Display u_7_segment_display_2 (
    .g(bcd_to_7_6_g), .f(bcd_to_7_6_f), .a(bcd_to_7_6_a_2), .b(bcd_to_7_6_b_2), .e(bcd_to_7_6_e),
    .d(bcd_to_7_6_d_2), .c(bcd_to_7_6_c_2));  // open: dp
  _7_Segment_Display u_7_segment_display_3 (
    .g(bcd_to_7_4_g), .f(bcd_to_7_4_f), .a(bcd_to_7_4_a_2), .b(bcd_to_7_4_b_2), .e(bcd_to_7_4_e),
    .d(bcd_to_7_4_d_2), .c(bcd_to_7_4_c_2));  // open: dp
  _7_Segment_Display u_7_segment_display_4 (
    .g(bcd_to_7_3_g), .f(bcd_to_7_3_f), .a(bcd_to_7_3_a_2), .b(bcd_to_7_3_b_2), .e(bcd_to_7_3_e),
    .d(bcd_to_7_3_d_2), .c(bcd_to_7_3_c_2));  // open: dp
  _7_Segment_Display u_7_segment_display_5 (
    .g(bcd_to_7_2_g), .f(bcd_to_7_2_f), .a(bcd_to_7_2_a_2), .b(bcd_to_7_2_b_2), .e(bcd_to_7_2_e),
    .d(bcd_to_7_2_d_2), .c(bcd_to_7_2_c_2));  // open: dp
  _7_Segment_Display u_7_segment_display_6 (
    .g(bcd_to_7_1_g), .f(bcd_to_7_1_f), .a(bcd_to_7_1_a_2), .b(bcd_to_7_1_b_2), .e(bcd_to_7_1_e),
    .d(bcd_to_7_1_d_2), .c(bcd_to_7_1_c_2));  // open: dp

  // Notes on the sheet:
  //   2107028
  //   2107027
  //   Digital clock
endmodule

module bcd_to_7 (
  input  A,
  input  B,
  input  C,
  input  D,
  output a_2,
  output b_2,
  output c_2,
  output d_2,
  output e,
  output f,
  output g
);

  wire A_B_out, A_prime_B_prime_out, A_prime_BC_prime_out, A_prime_C_out, AB_out, AB_prime_out, AC_out,
       AD_out, AD_prime_out, and_1_out, and_2_out, and_3_out, and_4_out, and_5_out, and_6_out, and_7_out,
       and_8_out, and_9_out, B_D_out, B_prime_C_out, B_prime_C_prime_2_out, B_prime_C_prime_out,
       B_prime_D_prime_out, BC_out, BD_out, BD_prime_out, C_prime_D_out, C_prime_D_prime_out, CD_prime_out,
       not_1_out, not_2_out, not_3_out, not_4_out, not_5_out, xnor_1_out, xor_1_out, xor_2_out;

  not not_1 (not_1_out, B);
  not not_2 (not_2_out, A);
  not not_3 (not_3_out, C);
  not not_4 (not_4_out, D);
  and B_prime_D_prime (B_prime_D_prime_out, not_4_out, not_1_out);
  and B_prime_C_prime (B_prime_C_prime_out, not_1_out, not_3_out);
  and AD_prime (AD_prime_out, not_4_out, A);
  and BD (BD_out, D, B);
  and A_prime_C (A_prime_C_out, not_2_out, C);
  and BC (BC_out, C, B);
  and A_prime_B_prime (A_prime_B_prime_out, not_2_out, not_1_out);
  and B_prime_C_prime_2 (B_prime_C_prime_2_out, not_1_out, not_3_out);
  xnor xnor_1 (xnor_1_out, C, D);
  xor A_B (A_B_out, A, B);
  and C_prime_D (C_prime_D_out, not_3_out, D);
  and B_D (B_D_out, not_1_out, D);
  xor xor_1 (xor_1_out, A, C);
  xor xor_2 (xor_2_out, B, C);
  and AB (AB_out, A, B);
  and AC (AC_out, A, C);
  and CD_prime (CD_prime_out, C, not_4_out);
  and C_prime_D_prime (C_prime_D_prime_out, not_3_out, not_4_out);
  and AB_prime (AB_prime_out, A, not_1_out);
  and A_prime_BC_prime (A_prime_BC_prime_out, not_2_out, B, not_3_out);
  and BD_prime (BD_prime_out, B, not_4_out);
  and AD (AD_out, A, D);
  and B_prime_C (B_prime_C_out, not_1_out, C);
  and and_1 (and_1_out, xnor_1_out, not_2_out);
  and and_2 (and_2_out, A, not_3_out, D);
  and and_3 (and_3_out, not_1_out, not_4_out);
  not not_5 (not_5_out, A_B_out);
  and and_4 (and_4_out, B_prime_C_prime_out, A);
  and and_5 (and_5_out, BD_out, not_2_out);
  and and_6 (and_6_out, not_5_out, not_4_out);
  and and_7 (and_7_out, xor_1_out, not_4_out);
  and and_8 (and_8_out, xor_2_out, D);
  and and_9 (and_9_out, B_prime_C_prime_2_out, AD_out);
  or u_a (a_2, B_prime_D_prime_out, and_4_out, AD_prime_out, and_5_out, A_prime_C_out, BC_out);
  or u_b (b_2, A_prime_B_prime_out, B_prime_C_prime_2_out, and_3_out, and_1_out, and_2_out);
  or u_c (c_2, B_prime_C_prime_out, A_B_out, C_prime_D_out, B_D_out);
  or u_d (d_2, and_6_out, and_7_out, and_9_out, and_8_out);
  or u_e (e, B_prime_D_prime_out, AB_out, AC_out, CD_prime_out);
  or u_f (f, AC_out, C_prime_D_prime_out, AB_prime_out, A_prime_BC_prime_out, BD_prime_out);
  or u_g (g, CD_prime_out, A_prime_BC_prime_out, AB_prime_out, AD_out, B_prime_C_out);

  // Notes on the sheet:
  //   2107028
  //   2107027
endmodule

module decade_counter (
  input  clock,
  output MSB,
  output out_3,
  output out_4,
  output LSB,
  output \and 
);

  wire not_1_out, not_2_out;

  T_Flip_Flop #(.trigger("falling")) t_ff_1 (
    .clk(clock), .T(1'b1), .Q(LSB), .preset(1'b0), .reset(\and ));  // open: Qn, en
  T_Flip_Flop #(.trigger("falling")) t_ff_2 (
    .clk(LSB), .T(1'b1), .Q(out_4), .preset(1'b0), .reset(\and ));  // open: Qn, en
  and and_1 (\and , MSB, not_1_out, out_4, not_2_out);
  T_Flip_Flop #(.trigger("falling")) t_ff_3 (
    .clk(out_4), .T(1'b1), .Q(out_3), .preset(1'b0), .reset(\and ));  // open: Qn, en
  not not_1 (not_1_out, out_3);
  not not_2 (not_2_out, LSB);
  T_Flip_Flop #(.trigger("falling")) t_ff_4 (
    .clk(out_3), .T(1'b1), .Q(MSB), .preset(1'b0), .reset(\and ));  // open: Qn, en

  // Notes on the sheet:
  //   2107028
  //   2107027
endmodule

module five_counter (
  input  clock,
  output MSB,
  output out_3,
  output out_4,
  output LSB
);

  wire and_1_out, not_1_out, not_2_out;

  T_Flip_Flop #(.trigger("falling")) t_ff_1 (
    .clk(clock), .T(1'b1), .Q(LSB), .preset(1'b0), .reset(and_1_out));  // open: Qn, en
  not not_1 (not_1_out, LSB);
  T_Flip_Flop #(.trigger("falling")) t_ff_2 (
    .clk(LSB), .T(1'b1), .Q(out_4), .preset(1'b0), .reset(and_1_out));  // open: Qn, en
  and and_1 (and_1_out, not_2_out, out_3, out_4, not_1_out);
  T_Flip_Flop #(.trigger("falling")) t_ff_3 (
    .clk(out_4), .T(1'b1), .Q(out_3), .preset(1'b0), .reset(and_1_out));  // open: Qn, en
  not not_2 (not_2_out, MSB);
  T_Flip_Flop #(.trigger("falling")) t_ff_4 (
    .clk(out_3), .T(1'b1), .Q(MSB), .preset(1'b0), .reset(and_1_out));  // open: Qn, en

  // Notes on the sheet:
  //   2107027
endmodule

module second (
  input  clock,
  output msb_10,
  output out_3,
  output out_4,
  output lsb_10,
  output msb_5,
  output out_7,
  output out_8,
  output lsb_5,
  output clock_puls_for_minute
);

  wire and_1_out, and_3_out, not_1_out, not_2_out, not_3_out, not_4_out, not_5_out, not_6_out, not_7_out,
       not_8_out, or_1_out;

  T_Flip_Flop #(.trigger("falling")) t_ff_1 (
    .clk(clock), .T(1'b1), .Q(lsb_10), .reset(or_1_out));  // open: Qn, preset, en
  T_Flip_Flop #(.trigger("falling")) t_ff_2 (
    .clk(lsb_10), .T(1'b1), .Q(out_4), .reset(or_1_out));  // open: Qn, preset, en
  or or_1 (or_1_out, and_1_out, and_3_out);
  T_Flip_Flop #(.trigger("falling")) t_ff_3 (
    .clk(and_1_out), .T(1'b1), .Q(lsb_5), .preset(1'b0), .reset(clock_puls_for_minute));  // open: Qn, en
  not not_1 (not_1_out, msb_10);
  T_Flip_Flop #(.trigger("falling")) t_ff_4 (
    .clk(out_4), .T(1'b1), .Q(out_3), .reset(or_1_out));  // open: Qn, preset, en
  and and_1 (and_1_out, msb_10, not_3_out, out_4, not_4_out);
  not not_2 (not_2_out, lsb_5);
  not not_3 (not_3_out, out_3);
  not not_4 (not_4_out, lsb_10);
  T_Flip_Flop #(.trigger("falling")) t_ff_5 (
    .clk(lsb_5), .T(1'b1), .Q(out_8), .preset(1'b0), .reset(clock_puls_for_minute));  // open: Qn, en
  T_Flip_Flop #(.trigger("falling")) t_ff_6 (
    .clk(out_3), .T(1'b1), .Q(msb_10), .preset(and_3_out), .reset(and_1_out));  // open: Qn, en
  and and_2 (clock_puls_for_minute, not_5_out, out_7, out_8, not_2_out);
  and and_3 (and_3_out, not_1_out, out_3, out_4, lsb_10, not_8_out, not_6_out, out_8, not_7_out);
  T_Flip_Flop #(.trigger("falling")) t_ff_7 (
    .clk(out_8), .T(1'b1), .Q(out_7), .preset(1'b0), .reset(clock_puls_for_minute));  // open: Qn, en
  not not_5 (not_5_out, msb_5);
  not not_6 (not_6_out, out_7);
  not not_7 (not_7_out, lsb_5);
  not not_8 (not_8_out, msb_5);
  T_Flip_Flop #(.trigger("falling")) t_ff_8 (
    .clk(out_7), .T(1'b1), .Q(msb_5), .preset(1'b0), .reset(clock_puls_for_minute));  // open: Qn, en

  // Notes on the sheet:
  //   2107028
  //   2107027
endmodule

module minute (
  input  clock,
  output msb_minute_10,
  output out_3,
  output out_4,
  output lsb_minute_10,
  output msb_minute_5,
  output out_7,
  output out_8,
  output lsb_minute_5,
  output clock_puls_for_hour
);

  wire and_1_out, and_3_out, not_1_out, not_2_out, not_3_out, not_4_out, not_5_out, not_6_out, not_7_out,
       not_8_out, or_1_out;

  T_Flip_Flop #(.trigger("falling")) t_ff_1 (
    .clk(clock), .T(1'b1), .Q(lsb_minute_10), .reset(or_1_out));  // open: Qn, preset, en
  T_Flip_Flop #(.trigger("falling")) t_ff_2 (
    .clk(lsb_minute_10), .T(1'b1), .Q(out_4), .reset(or_1_out));  // open: Qn, preset, en
  or or_1 (or_1_out, and_1_out, and_3_out);
  T_Flip_Flop #(.trigger("falling")) t_ff_3 (
    .clk(and_1_out), .T(1'b1), .Q(lsb_minute_5), .preset(1'b0), .reset(clock_puls_for_hour));  // open: Qn, en
  not not_1 (not_1_out, msb_minute_10);
  T_Flip_Flop #(.trigger("falling")) t_ff_4 (
    .clk(out_4), .T(1'b1), .Q(out_3), .reset(or_1_out));  // open: Qn, preset, en
  and and_1 (and_1_out, msb_minute_10, not_3_out, out_4, not_4_out);
  not not_2 (not_2_out, lsb_minute_5);
  not not_3 (not_3_out, out_3);
  not not_4 (not_4_out, lsb_minute_10);
  T_Flip_Flop #(.trigger("falling")) t_ff_5 (
    .clk(lsb_minute_5), .T(1'b1), .Q(out_8), .preset(1'b0), .reset(clock_puls_for_hour));  // open: Qn, en
  T_Flip_Flop #(.trigger("falling")) t_ff_6 (
    .clk(out_3), .T(1'b1), .Q(msb_minute_10), .preset(and_3_out), .reset(and_1_out));  // open: Qn, en
  and and_2 (clock_puls_for_hour, not_5_out, out_7, out_8, not_2_out);
  and and_3 (and_3_out, not_1_out, out_3, out_4, lsb_minute_10, not_8_out, not_6_out, out_8, not_7_out);
  T_Flip_Flop #(.trigger("falling")) t_ff_7 (
    .clk(out_8), .T(1'b1), .Q(out_7), .preset(1'b0), .reset(clock_puls_for_hour));  // open: Qn, en
  not not_5 (not_5_out, msb_minute_5);
  not not_6 (not_6_out, out_7);
  not not_7 (not_7_out, lsb_minute_5);
  not not_8 (not_8_out, msb_minute_5);
  T_Flip_Flop #(.trigger("falling")) t_ff_8 (
    .clk(out_7), .T(1'b1), .Q(msb_minute_5), .preset(1'b0), .reset(clock_puls_for_hour));  // open: Qn, en

  // Notes on the sheet:
  //   2107028
  //   2107027
endmodule

module hour (
  input  clock,
  output MSB_right,
  output out_3,
  output out_4,
  output LSB_right,
  output MSB_left,
  output out_7,
  output out_8,
  output LSB_right_2
);

  wire and_1_out, and_2_out, and_3_out, not_1_out, not_2_out, not_3_out, not_4_out, not_5_out, not_6_out,
       not_7_out, not_8_out, not_9_out, or_1_out, or_2_out;

  and and_1 (and_1_out, not_4_out, not_5_out, not_6_out, LSB_right_2, not_7_out, not_1_out, out_4, LSB_right);
  T_Flip_Flop #(.trigger("falling")) t_ff_1 (
    .clk(clock), .T(1'b1), .Q(LSB_right), .preset(and_1_out), .reset(and_2_out));  // open: Qn, en
  or or_1 (or_1_out, and_1_out, and_2_out);
  T_Flip_Flop #(.trigger("falling")) t_ff_2 (
    .clk(and_2_out), .T(1'b1), .Q(LSB_right_2), .reset(or_2_out));  // open: Qn, preset, en
  or or_2 (or_2_out, and_1_out, and_3_out);
  T_Flip_Flop #(.trigger("falling")) t_ff_3 (
    .clk(LSB_right), .T(1'b1), .Q(out_4), .reset(or_1_out));  // open: Qn, preset, en
  and and_2 (and_2_out, MSB_right, not_2_out, out_4, not_3_out);
  T_Flip_Flop #(.trigger("falling")) t_ff_4 (
    .clk(LSB_right_2), .T(1'b1), .Q(out_8), .reset(or_2_out));  // open: Qn, preset, en
  not not_1 (not_1_out, out_3);
  and and_3 (and_3_out, MSB_left, not_8_out, out_8, not_9_out);
  T_Flip_Flop #(.trigger("falling")) t_ff_5 (
    .clk(out_4), .T(1'b1), .Q(out_3), .reset(or_1_out));  // open: Qn, preset, en
  not not_2 (not_2_out, out_3);
  not not_3 (not_3_out, LSB_right);
  T_Flip_Flop #(.trigger("falling")) t_ff_6 (
    .clk(out_8), .T(1'b1), .Q(out_7), .reset(or_2_out));  // open: Qn, preset, en
  not not_4 (not_4_out, MSB_left);
  not not_5 (not_5_out, out_7);
  not not_6 (not_6_out, out_8);
  not not_7 (not_7_out, MSB_right);
  not not_8 (not_8_out, out_7);
  not not_9 (not_9_out, LSB_right_2);
  T_Flip_Flop #(.trigger("falling")) t_ff_7 (
    .clk(out_3), .T(1'b1), .Q(MSB_right), .reset(or_1_out));  // open: Qn, preset, en
  T_Flip_Flop #(.trigger("falling")) t_ff_8 (
    .clk(out_7), .T(1'b1), .Q(MSB_left), .reset(or_2_out));  // open: Qn, preset, en

  // Notes on the sheet:
  //   2107027
  //   2107028
endmodule
