// Logisim project Comparator.circ as structural Verilog: 4 circuits, main circuit main
module main (
  input  [3:0] A,
  input  [3:0] B,
  output A_B,
  output A_B_2,
  output A_B_3
);

  _4_Bit_Comparator u_4_bit_comparator_1 (
    .A3(A[3]), .B3(B[3]), .A2(A[2]), .B2(B[2]), .A1(A[1]), .B1(B[1]), .A0(A[0]), .B0(B[0]), .A_B(A_B),
    .A_B_2(A_B_2), .A_B_3(A_B_3));

  // Notes on the sheet:
  //   ROLL 2107027
endmodule

module _1_Bit_Comparator (
  input  A,
  input  B,
  output A_B,
  output A_B_2,
  output A_B_3
);

  wire not_1_out, not_2_out, or_1_out;

  not not_1 (not_1_out, A);
  not not_2 (not_2_out, B);
  and AB_prime (A_B, A, not_2_out);
  and A_prime_B (A_B_3, not_1_out, B);
  or or_1 (or_1_out, A_B, A_B_3);
  not not_3 (A_B_2, or_1_out);

  // Notes on the sheet:
  //   Roll  2107027
endmodule

module _2_Bit_Comparator (
  input  A1,
  input  B1,
  input  A0,
  input  B0,
  output out_5,
  output out_6,
  output out_7
);

  wire and_1_out, and_2_out, n1_bit_comparator_1_a_b, n1_bit_comparator_1_a_b_2, n1_bit_comparator_1_a_b_3,
       n1_bit_comparator_2_a_b, n1_bit_comparator_2_a_b_2, n1_bit_comparator_2_a_b_3;

  _1_Bit_Comparator u_1_bit_comparator_1 (
    .A(A1), .B(B1), .A_B(n1_bit_comparator_1_a_b), .A_B_2(n1_bit_comparator_1_a_b_2),
    .A_B_3(n1_bit_comparator_1_a_b_3));
  _1_Bit_Comparator u_1_bit_comparator_2 (
    .A(A0), .B(B0), .A_B(n1_bit_comparator_2_a_b), .A_B_2(n1_bit_comparator_2_a_b_2),
    .A_B_3(n1_bit_comparator_2_a_b_3));
  and and_1 (and_1_out, n1_bit_comparator_1_a_b_2, n1_bit_comparator_2_a_b);
  and and_2 (and_2_out, n1_bit_comparator_1_a_b_2, n1_bit_comparator_2_a_b_3);
  or or_1 (out_5, n1_bit_comparator_1_a_b, and_1_out);
  and and_3 (out_6, n1_bit_comparator_1_a_b_2, n1_bit_comparator_2_a_b_2);
  or or_2 (out_7, and_2_out, n1_bit_comparator_1_a_b_3);

  // Notes on the sheet:
  //   Roll 2107027
  //   A>B
  //   A=B
  //   A<B
endmodule

module _4_Bit_Comparator (
  input  A3,
  input  B3,
  input  A2,
  input  B2,
  input  A1,
  input  B1,
  input  A0,
  input  B0,
  output A_B,
  output A_B_2,
  output A_B_3
);

  wire and_1_out, and_2_out, n2_bit_comparator_1_out_5, n2_bit_comparator_1_out_6, n2_bit_comparator_1_out_7,
       n2_bit_comparator_2_out_5, n2_bit_comparator_2_out_6, n2_bit_comparator_2_out_7;

  _2_Bit_Comparator u_2_bit_comparator_1 (
    .A1(A3), .B1(B3), .A0(A2), .B0(B2), .out_5(n2_bit_comparator_1_out_5), .out_6(n2_bit_comparator_1_out_6),
    .out_7(n2_bit_comparator_1_out_7));
  _2_Bit_Comparator u_2_bit_comparator_2 (
    .A1(A1), .B1(B1), .A0(A0), .B0(B0), .out_5(n2_bit_comparator_2_out_5), .out_6(n2_bit_comparator_2_out_6),
    .out_7(n2_bit_comparator_2_out_7));
  and and_1 (and_1_out, n2_bit_comparator_2_out_5, n2_bit_comparator_1_out_6);
  and and_2 (and_2_out, n2_bit_comparator_2_out_7, n2_bit_comparator_1_out_6);
  or or_1 (A_B, n2_bit_comparator_1_out_5, and_1_out);
  and and_3 (A_B_2, n2_bit_comparator_1_out_6, n2_bit_comparator_2_out_6);
  or or_2 (A_B_3, and_2_out, n2_bit_comparator_1_out_7);

  // Notes on the sheet:
  //   ROll 2107027
endmodule
