// Logisim project Down_Counter.circ as structural Verilog: 1 circuit, main circuit main
module main (
  output A,
  output B,
  output C
);

  wire and_1_out, and_2_out, and_3_out, and_4_out, and_5_out, clock_1_out, d_ff_1_qn, d_ff_2_qn, d_ff_3_qn,
       or_1_out, or_2_out;

  and and_1 (and_1_out, and_2_out, d_ff_1_qn);
  and and_2 (and_2_out, d_ff_3_qn, d_ff_2_qn);
  Clock clock_1 (.out(clock_1_out));
  or or_1 (or_1_out, and_1_out, and_4_out, and_3_out);
  or or_2 (or_2_out, and_2_out, and_5_out);
  D_Flip_Flop d_ff_1 (.clk(clock_1_out), .D(or_1_out), .Q(A), .Qn(d_ff_1_qn));  // open: preset, en, reset
  and and_3 (and_3_out, A, B);
  and and_4 (and_4_out, A, C);
  D_Flip_Flop d_ff_2 (.clk(clock_1_out), .D(or_2_out), .Q(B), .Qn(d_ff_2_qn));  // open: preset, en, reset
  and and_5 (and_5_out, B, C);
  D_Flip_Flop d_ff_3 (.clk(clock_1_out), .D(d_ff_3_qn), .Q(C), .Qn(d_ff_3_qn));  // open: preset, en, reset

  // Notes on the sheet:
  //   Roll 2107027
  //   A
  //   B
  //   C
endmodule
